// Logisim project Lab3.circ as structural Verilog
module one_bit_ALU (
  input  [3:0] ALU_CTRL,
  input  A,
  input  B,
  input  C,
  output R,
  output C_out
);

  wire and_1_out, multiplexer_1_out, not_1_out, one_bit_adder_1_s, or_1_out, xor_1_out;

  not not_1 (not_1_out, B);
  Multiplexer #(.enable("false")) multiplexer_1 (.in0(B), .in1(not_1_out), .out(multiplexer_1_out), .sel(ALU_CTRL[2]));
  and and_1 (and_1_out, A, multiplexer_1_out);
  or or_1 (or_1_out, A, multiplexer_1_out);
  xor xor_1 (xor_1_out, A, multiplexer_1_out);
  One_bit_adder one_bit_adder_1 (.A(A), .B(multiplexer_1_out), .C(C), .S(one_bit_adder_1_s), .C_out(C_out));
  Multiplexer #(.enable("false"), .select(2)) multiplexer_2 (
    .in0(and_1_out), .in1(or_1_out), .in2(xor_1_out), .in3(one_bit_adder_1_s), .out(R), .sel(ALU_CTRL[1:0]));
endmodule

module One_bit_adder (
  input  A,
  input  B,
  input  C,
  output S,
  output C_out
);

  wire and_1_out, and_2_out, xor_1_out;

  xor xor_1 (xor_1_out, A, B);
  xor xor_2 (S, xor_1_out, C);
  and and_1 (and_1_out, xor_1_out, C);
  and and_2 (and_2_out, A, B);
  or or_1 (C_out, and_1_out, and_2_out);
endmodule

module ALU_CTR_Circut (
  input  I30,
  input  I14,
  input  I13,
  input  I12,
  input  I6,
  input  I5,
  input  I4,
  output ALU_CtrI3,
  output ALU_CtrI2,
  output ALU_CtrI1,
  output ALU_CtrI0,
  output ALU_Src
);

  wire and_2_out, and_3_out, and_4_out, and_5_out, and_6_out, not_1_out, not_2_out, not_3_out, not_4_out,
       not_5_out, not_6_out;

  not not_1 (not_1_out, I30);
  not not_2 (not_2_out, I14);
  not not_3 (not_3_out, I13);
  not not_4 (not_4_out, I12);
  not not_5 (not_5_out, I5);
  not not_6 (not_6_out, I4);
  and and_1 (ALU_CtrI2, I30, not_2_out, not_3_out);
  or or_1 (ALU_CtrI1, not_2_out, not_3_out);
  and and_2 (and_2_out, I13, not_4_out);
  and and_3 (and_3_out, I30, not_2_out);
  and and_4 (and_4_out, not_1_out, not_5_out);
  and and_5 (and_5_out, I13, not_5_out);
  and and_6 (and_6_out, I14, not_5_out);
  or or_2 (ALU_CtrI0, and_2_out, and_3_out);
  or or_3 (ALU_Src, and_4_out, not_6_out, and_5_out, and_6_out);

  assign ALU_CtrI3 = 1'b0;
endmodule

module ALU4 (
  input  [3:0] ALU_Ctr,
  input  [3:0] A,
  input  [3:0] B,
  input  C,
  output [3:0] R,
  output C_out
);

  wire one_bit_alu_1_c_out, one_bit_alu_2_c_out, one_bit_alu_3_c_out;

  one_bit_ALU one_bit_alu_1 (.ALU_CTRL(ALU_Ctr), .A(A[0]), .B(B[0]), .C(C), .R(R[0]), .C_out(one_bit_alu_1_c_out));
  one_bit_ALU one_bit_alu_2 (
    .ALU_CTRL(ALU_Ctr), .A(A[1]), .B(B[1]), .C(one_bit_alu_1_c_out), .R(R[1]), .C_out(one_bit_alu_2_c_out));
  one_bit_ALU one_bit_alu_3 (
    .ALU_CTRL(ALU_Ctr), .A(A[2]), .B(B[2]), .C(one_bit_alu_2_c_out), .R(R[2]), .C_out(one_bit_alu_3_c_out));
  one_bit_ALU one_bit_alu_4 (.ALU_CTRL(ALU_Ctr), .A(A[3]), .B(B[3]), .C(one_bit_alu_3_c_out), .R(R[3]), .C_out(C_out));
endmodule

module ALU32 (
  input  [3:0] ALU_CtrI,
  input  [31:0] in_2,
  input  [31:0] in_3,
  output [31:0] Result,
  output C_out
);

  wire alu4_1_c_out, alu4_2_c_out, alu4_3_c_out, alu4_4_c_out, alu4_5_c_out, alu4_6_c_out, alu4_8_c_out;

  ALU4 alu4_1 (
    .ALU_Ctr(ALU_CtrI), .A(in_2[3:0]), .B(in_3[3:0]), .C(ALU_CtrI[2]), .R(Result[3:0]), .C_out(alu4_1_c_out));
  ALU4 alu4_2 (
    .ALU_Ctr(ALU_CtrI), .A(in_2[7:4]), .B(in_3[7:4]), .C(alu4_1_c_out), .R(Result[7:4]), .C_out(alu4_2_c_out));
  ALU4 alu4_3 (
    .ALU_Ctr(ALU_CtrI), .A(in_2[11:8]), .B(in_3[11:8]), .C(alu4_2_c_out), .R(Result[11:8]),
    .C_out(alu4_3_c_out));
  ALU4 alu4_4 (
    .ALU_Ctr(ALU_CtrI), .A(in_2[15:12]), .B(in_3[15:12]), .C(alu4_3_c_out), .R(Result[15:12]),
    .C_out(alu4_4_c_out));
  ALU4 alu4_5 (
    .ALU_Ctr(ALU_CtrI), .A(in_2[23:20]), .B(in_3[23:20]), .C(alu4_8_c_out), .R(Result[23:20]),
    .C_out(alu4_5_c_out));
  ALU4 alu4_6 (
    .ALU_Ctr(ALU_CtrI), .A(in_2[27:24]), .B(in_3[27:24]), .C(alu4_5_c_out), .R(Result[27:24]),
    .C_out(alu4_6_c_out));
  ALU4 alu4_7 (
    .ALU_Ctr(ALU_CtrI), .A(in_2[31:28]), .B(in_3[31:28]), .C(alu4_6_c_out), .R(Result[31:28]), .C_out(C_out));
  ALU4 alu4_8 (
    .ALU_Ctr(ALU_CtrI), .A(in_2[19:16]), .B(in_3[19:16]), .C(alu4_4_c_out), .R(Result[19:16]),
    .C_out(alu4_8_c_out));
endmodule
