// Logisim project Lab4_cir.circ as structural Verilog: 4 circuits, main circuit Imm_Gem
module Imm_Gem (
  input  [31:0] Instr,
  output [31:0] IMM32
);

  Multiplexer #(.enable("false"), .select(2)) multiplexer_1 (
    .in0(Instr[20]), .in1(Instr[7]), .in2(1'b0), .out(IMM32[0]), .sel(Instr[6:5]));  // open: in3
  Multiplexer #(.enable("false"), .width(4)) multiplexer_2 (
    .in0(Instr[24:21]), .in1(Instr[11:8]), .out(IMM32[4:1]), .sel(Instr[5]));
  Multiplexer #(.enable("false")) multiplexer_3 (.in0(Instr[31]), .in1(Instr[7]), .out(IMM32[11]), .sel(Instr[6]));
  assign IMM32[31:12] = {{19{Instr[31]}}, Instr[31]};  // Bit_Extender bit_extender_1

  assign IMM32[10:5] = Instr[30:25];

  // Other names for the same wires on the sheet: I30_25[5:0] = Instr[30:25]; I5 = Instr[5]; I6_5[1:0] = Instr[6:5];
  //   I6 = Instr[6]; I7 = Instr[7]; I11_8[3:0] = Instr[11:8]; I_20 = Instr[20]; I24_21[3:0] = Instr[24:21];
  //   I31 = Instr[31]
endmodule

module ALucontrol (
  input  I6,
  input  I5,
  input  I4,
  input  I3,
  input  I2,
  input  I1,
  input  I0,
  output MemoryToRegis,
  output MemRead,
  output MemoryRead,
  output MemWrite,
  output Branch
);

  wire not_1_out, not_2_out;

  not not_1 (not_1_out, I0);
  not not_2 (not_2_out, I0);
  not not_3 (MemoryToRegis, I0);
  or or_1 (MemRead, not_2_out, I0);
  and and_1 (MemoryRead, not_2_out, MemoryToRegis);
  and and_2 (MemWrite, not_1_out, I0, MemoryToRegis);

  assign Branch = I0;
  assign I1 = I0;
  assign I2 = I0;
  assign I3 = I0;
  assign I4 = I0;
  assign I5 = I0;
  assign I6 = I0;
endmodule

module Instruction_Memory (
  input  [23:0] Addr,
  input  clockin,
  output [31:0] Instr
);

  wire not_1_out;
  wire [31:0] undriven;

  not not_1 (not_1_out, clockin);
  RAM #(.addrWidth(22), .asyncread("true"), .dataWidth(32)) ram_1 (
    .addr(Addr[23:2]), .we(1'b0), .oe(not_1_out), .din(undriven), .dout(Instr));  // open: clk
endmodule

module Data_Memory (
  input  [25:0] Addr,
  input  Memorywrite,
  input  Memoryread,
  input  clockin,
  input  [31:0] Write_data,
  output [31:0] Instr
);

  RAM #(.addrWidth(24), .dataWidth(32)) ram_1 (
    .addr(Addr[25:2]), .we(Memorywrite), .oe(Memoryread), .clk(clockin), .din(Write_data), .dout(Instr));
endmodule
