// Logisim project lab4.circ as structural Verilog: 13 circuits, main circuit main
module main (
);

  wire alu_control_circuit_1_alu_src, and_1_out, clock_1_out, comparator_1_eq, ctr_1_branch, ctr_1_mtoreg,
       ctr_1_mwrite, ctr_1_read, ctr_1_rwrite;
  wire [3:0] alu_control_circuit_1_alu_ctrl0;
  wire [4:0] in_memory_1_instr_2, in_memory_1_instr_4, in_memory_1_instr_5;
  wire [6:0] in_memory_1_instr;
  wire [7:0] register_1_q_2;
  wire [23:0] register_1_q;
  wire [25:0] undriven;
  wire [31:0] adder_1_out, adder_2_out, alu32_1_result, datamem_1_instr, mmg_1_imm32, multiplexer_1_out,
       multiplexer_2_out, multiplexer_3_out, register_file_1_r_data1, register_file_1_r_data2;
  wire [31:12] in_memory_1_instr_3;

  Register #(.width(32)) register_1 (
    .D(multiplexer_2_out), .en(1'b1), .clk(clock_1_out), .Q({register_1_q_2, register_1_q}));  // open: clr
  Clock clock_1 (.out(clock_1_out));
  Adder #(.width(32)) adder_1 (.a({register_1_q_2, register_1_q}), .b(32'h4), .out(adder_1_out));  // open: cin, cout
  In_memory in_memory_1 (
    .address(register_1_q), .clock_in(clock_1_out),
    .Instr({in_memory_1_instr_3[31:25], in_memory_1_instr_5, in_memory_1_instr_4, in_memory_1_instr_3[14:12], in_memory_1_instr_2, in_memory_1_instr}));
  ctr ctr_1 (
    .I6(in_memory_1_instr), .Mtoreg(ctr_1_mtoreg), .RWrite(ctr_1_rwrite), .Read(ctr_1_read),
    .MWrite(ctr_1_mwrite), .Branch(ctr_1_branch));
  mmG mmg_1 (
    .Instr({in_memory_1_instr_3[31:25], in_memory_1_instr_5, in_memory_1_instr_4, in_memory_1_instr_3[14:12], in_memory_1_instr_2, in_memory_1_instr}),
    .IMM32(mmg_1_imm32));
  Register_File register_file_1 (
    .R_Reg2(in_memory_1_instr_4), .WData(multiplexer_3_out), .R_Reg1(in_memory_1_instr_5),
    .Clock_in(clock_1_out), .Write(ctr_1_rwrite), .WReg(in_memory_1_instr_2),
    .R_Data1(register_file_1_r_data1), .R_Data2(register_file_1_r_data2));
  Adder #(.width(32)) adder_2 (
    .a({register_1_q_2, register_1_q}), .b(mmg_1_imm32), .out(adder_2_out));  // open: cin, cout
  Multiplexer #(.enable("false"), .width(32)) multiplexer_1 (
    .in0(register_file_1_r_data2), .in1(mmg_1_imm32), .out(multiplexer_1_out),
    .sel(alu_control_circuit_1_alu_src));
  ALU_Control_circuit alu_control_circuit_1 (
    .I30(in_memory_1_instr_3[30]), .I14(in_memory_1_instr_3[14]), .I13(in_memory_1_instr_3[13]),
    .I12(in_memory_1_instr_3[12]), .I6(in_memory_1_instr[6]), .I5(in_memory_1_instr[5]),
    .I4(in_memory_1_instr[4]), .ALU_Ctrl3(alu_control_circuit_1_alu_ctrl0[3]),
    .ALU_Ctrl2(alu_control_circuit_1_alu_ctrl0[2]), .ALU_Ctrl1(alu_control_circuit_1_alu_ctrl0[1]),
    .ALU_Ctrl0(alu_control_circuit_1_alu_ctrl0[0]), .ALU_Src(alu_control_circuit_1_alu_src));
  Comparator #(.width(32)) comparator_1 (
    .a(register_file_1_r_data1), .b(register_file_1_r_data2), .eq(comparator_1_eq));  // open: gt, lt
  and and_1 (and_1_out, ctr_1_branch, comparator_1_eq);
  Multiplexer #(.enable("false"), .width(32)) multiplexer_2 (
    .in0(adder_1_out), .in1(adder_2_out), .out(multiplexer_2_out), .sel(and_1_out));
  ALU32 alu32_1 (
    .ALU_Ctrl(alu_control_circuit_1_alu_ctrl0), .A(register_file_1_r_data1), .B(multiplexer_1_out),
    .Result(alu32_1_result));  // open: C_Out
  DataMem datamem_1 (
    .address(undriven), .Write(ctr_1_read), .Memoryread(ctr_1_mwrite), .clockin(clock_1_out),
    .WD(register_file_1_r_data2), .Instr(datamem_1_instr));
  Multiplexer #(.enable("false"), .width(32)) multiplexer_3 (
    .in0(alu32_1_result), .in1(datamem_1_instr), .out(multiplexer_3_out), .sel(ctr_1_mtoreg));
endmodule

module one_bit_ALU (
  input  [3:0] ALU_Ctrl,
  input  A,
  input  B,
  input  C_in,
  output R,
  output C_out
);

  wire and_1_out, multiplexer_1_out, not_1_out, one_bit_adder_1_s, or_1_out, xor_1_out;

  Multiplexer #(.enable("false")) multiplexer_1 (.in0(B), .in1(not_1_out), .out(multiplexer_1_out), .sel(ALU_Ctrl[2]));
  not not_1 (not_1_out, B);
  and and_1 (and_1_out, A, multiplexer_1_out);
  or or_1 (or_1_out, A, multiplexer_1_out);
  xor xor_1 (xor_1_out, A, multiplexer_1_out);
  one_bit_adder one_bit_adder_1 (.A(A), .B(multiplexer_1_out), .C(C_in), .S(one_bit_adder_1_s), .C_out(C_out));
  Multiplexer #(.enable("false"), .select(2)) multiplexer_2 (
    .in0(and_1_out), .in1(or_1_out), .in2(xor_1_out), .in3(one_bit_adder_1_s), .out(R), .sel(ALU_Ctrl[1:0]));
endmodule

module one_bit_adder (
  input  A,
  input  B,
  input  C,
  output S,
  output C_out
);

  wire and_1_out, and_2_out, xor_1_out;

  xor xor_1 (xor_1_out, A, B);
  xor xor_2 (S, xor_1_out, C);
  and and_1 (and_1_out, xor_1_out, C);
  and and_2 (and_2_out, A, B);
  or or_1 (C_out, and_1_out, and_2_out);
endmodule

module ALU_Control_circuit (
  input  I30,
  input  I14,
  input  I13,
  input  I12,
  input  I6,
  input  I5,
  input  I4,
  output ALU_Ctrl3,
  output ALU_Ctrl2,
  output ALU_Ctrl1,
  output ALU_Ctrl0,
  output ALU_Src
);

  wire and_2_out, and_3_out, not_1_out, not_2_out, not_3_out, not_4_out, not_5_out, not_6_out;

  not not_1 (not_1_out, I14);
  not not_2 (not_2_out, I13);
  not not_3 (not_3_out, I12);
  not not_4 (not_4_out, I6);
  not not_5 (not_5_out, I5);
  not not_6 (not_6_out, I4);
  and and_1 (ALU_Ctrl2, I30, not_2_out, I5);
  or or_1 (ALU_Ctrl1, not_2_out, not_6_out);
  and and_2 (and_2_out, I13, not_3_out);
  and and_3 (and_3_out, not_4_out, not_6_out);
  or or_2 (ALU_Ctrl0, not_1_out, and_2_out);
  or or_3 (ALU_Src, and_3_out, not_5_out);

  assign ALU_Ctrl3 = 1'b0;
endmodule

module ALU4 (
  input  [3:0] ALU_Ctrl,
  input  [3:0] A,
  input  [3:0] B,
  input  C_in,
  output [3:0] R,
  output C_out
);

  wire one_bit_alu_1_c_out, one_bit_alu_2_c_out, one_bit_alu_3_c_out;

  one_bit_ALU one_bit_alu_1 (
    .ALU_Ctrl(ALU_Ctrl), .A(A[0]), .B(B[0]), .C_in(C_in), .R(R[0]), .C_out(one_bit_alu_1_c_out));
  one_bit_ALU one_bit_alu_2 (
    .ALU_Ctrl(ALU_Ctrl), .A(A[1]), .B(B[1]), .C_in(one_bit_alu_1_c_out), .R(R[1]), .C_out(one_bit_alu_2_c_out));
  one_bit_ALU one_bit_alu_3 (
    .ALU_Ctrl(ALU_Ctrl), .A(A[2]), .B(B[2]), .C_in(one_bit_alu_2_c_out), .R(R[2]), .C_out(one_bit_alu_3_c_out));
  one_bit_ALU one_bit_alu_4 (
    .ALU_Ctrl(ALU_Ctrl), .A(A[3]), .B(B[3]), .C_in(one_bit_alu_3_c_out), .R(R[3]), .C_out(C_out));
endmodule

module ALU32 (
  input  [3:0] ALU_Ctrl,
  input  [31:0] A,
  input  [31:0] B,
  output [31:0] Result,
  output C_Out
);

  wire alu4_1_c_out, alu4_2_c_out, alu4_3_c_out, alu4_4_c_out, alu4_5_c_out, alu4_6_c_out, alu4_7_c_out;

  ALU4 alu4_1 (.ALU_Ctrl(ALU_Ctrl), .A(A[3:0]), .B(B[3:0]), .C_in(ALU_Ctrl[2]), .R(Result[3:0]), .C_out(alu4_1_c_out));
  ALU4 alu4_2 (.ALU_Ctrl(ALU_Ctrl), .A(A[7:4]), .B(B[7:4]), .C_in(alu4_1_c_out), .R(Result[7:4]), .C_out(alu4_2_c_out));
  ALU4 alu4_3 (
    .ALU_Ctrl(ALU_Ctrl), .A(A[11:8]), .B(B[11:8]), .C_in(alu4_2_c_out), .R(Result[11:8]), .C_out(alu4_3_c_out));
  ALU4 alu4_4 (
    .ALU_Ctrl(ALU_Ctrl), .A(A[15:12]), .B(B[15:12]), .C_in(alu4_3_c_out), .R(Result[15:12]),
    .C_out(alu4_4_c_out));
  ALU4 alu4_5 (
    .ALU_Ctrl(ALU_Ctrl), .A(A[19:16]), .B(B[23:20]), .C_in(alu4_4_c_out), .R(Result[19:16]),
    .C_out(alu4_5_c_out));
  ALU4 alu4_6 (
    .ALU_Ctrl(ALU_Ctrl), .A(A[23:20]), .B(B[23:20]), .C_in(alu4_5_c_out), .R(Result[23:20]),
    .C_out(alu4_6_c_out));
  ALU4 alu4_7 (
    .ALU_Ctrl(ALU_Ctrl), .A(A[27:24]), .B(B[27:24]), .C_in(alu4_6_c_out), .R(Result[27:24]),
    .C_out(alu4_7_c_out));
  ALU4 alu4_8 (.ALU_Ctrl(ALU_Ctrl), .A(A[31:28]), .B(B[31:28]), .C_in(alu4_7_c_out), .R(Result[31:28]), .C_out(C_Out));

  assign B[19:16] = B[23:20];
endmodule

module Register_File (
  input  [4:0] R_Reg2,
  input  [31:0] WData,
  input  [4:0] R_Reg1,
  input  Clock_in,
  input  Write,
  input  [4:0] WReg,
  output [31:0] R_Data1,
  output [31:0] R_Data2
);

  wire demultiplexer_1_out0, demultiplexer_1_out1, demultiplexer_1_out2, demultiplexer_1_out3,
       demultiplexer_1_out4, demultiplexer_1_out5, demultiplexer_1_out6, demultiplexer_1_out7,
       demultiplexer_1_out8, demultiplexer_1_out9, demultiplexer_1_out10, demultiplexer_1_out11,
       demultiplexer_1_out12, demultiplexer_1_out13, demultiplexer_1_out14, demultiplexer_1_out15,
       demultiplexer_1_out16, demultiplexer_1_out17, demultiplexer_1_out18, demultiplexer_1_out19,
       demultiplexer_1_out20, demultiplexer_1_out21, demultiplexer_1_out22, demultiplexer_1_out23,
       demultiplexer_1_out24, demultiplexer_1_out25, demultiplexer_1_out26, demultiplexer_1_out27,
       demultiplexer_1_out28, demultiplexer_1_out29, demultiplexer_1_out30, demultiplexer_1_out31;
  wire [31:0] Q0, Q1, Q2, Q3, Q4, Q5, Q6, Q7, Q8, Q9, Q10, Q11, Q12, Q13, Q14, Q15, Q16, Q17, Q18, Q19, Q20,
       Q21, Q22, Q23, Q24, Q25, Q26, Q27, Q28, Q29, Q30, Q31;

  Demultiplexer #(.enable("false"), .select(5)) demultiplexer_1 (
    .out0(demultiplexer_1_out0), .out1(demultiplexer_1_out1), .out2(demultiplexer_1_out2),
    .out3(demultiplexer_1_out3), .out4(demultiplexer_1_out4), .out5(demultiplexer_1_out5),
    .out6(demultiplexer_1_out6), .out7(demultiplexer_1_out7), .out8(demultiplexer_1_out8),
    .out9(demultiplexer_1_out9), .out10(demultiplexer_1_out10), .out11(demultiplexer_1_out11),
    .out12(demultiplexer_1_out12), .out13(demultiplexer_1_out13), .out14(demultiplexer_1_out14),
    .out15(demultiplexer_1_out15), .out16(demultiplexer_1_out16), .out17(demultiplexer_1_out17),
    .out18(demultiplexer_1_out18), .out19(demultiplexer_1_out19), .out20(demultiplexer_1_out20),
    .out21(demultiplexer_1_out21), .out22(demultiplexer_1_out22), .out23(demultiplexer_1_out23),
    .out24(demultiplexer_1_out24), .out25(demultiplexer_1_out25), .out26(demultiplexer_1_out26),
    .out27(demultiplexer_1_out27), .out28(demultiplexer_1_out28), .out29(demultiplexer_1_out29),
    .out30(demultiplexer_1_out30), .out31(demultiplexer_1_out31), .in(Write), .sel(WReg));
  Register #(.width(32)) register_1 (.D(WData), .en(demultiplexer_1_out0), .clk(Clock_in), .Q(Q0), .clr(Write));
  Register #(.width(32)) register_2 (.D(WData), .en(demultiplexer_1_out1), .clk(Clock_in), .Q(Q1));  // open: clr
  Register #(.width(32)) register_3 (.D(WData), .en(demultiplexer_1_out2), .clk(Clock_in), .Q(Q2));  // open: clr
  Register #(.width(32)) register_4 (.D(WData), .en(demultiplexer_1_out3), .clk(Clock_in), .Q(Q3));  // open: clr
  Register #(.width(32)) register_5 (.D(WData), .en(demultiplexer_1_out4), .clk(Clock_in), .Q(Q4));  // open: clr
  Register #(.width(32)) register_6 (.D(WData), .en(demultiplexer_1_out5), .clk(Clock_in), .Q(Q5));  // open: clr
  Register #(.width(32)) register_7 (.D(WData), .en(demultiplexer_1_out6), .clk(Clock_in), .Q(Q6));  // open: clr
  Register #(.width(32)) register_8 (.D(WData), .en(demultiplexer_1_out7), .clk(Clock_in), .Q(Q7));  // open: clr
  Register #(.width(32)) register_9 (.D(WData), .en(demultiplexer_1_out8), .clk(Clock_in), .Q(Q8));  // open: clr
  Register #(.width(32)) register_10 (.D(WData), .en(demultiplexer_1_out9), .clk(Clock_in), .Q(Q9));  // open: clr
  Register #(.width(32)) register_11 (.D(WData), .en(demultiplexer_1_out10), .clk(Clock_in), .Q(Q10));  // open: clr
  Register #(.width(32)) register_12 (.D(WData), .en(demultiplexer_1_out11), .clk(Clock_in), .Q(Q11));  // open: clr
  Register #(.width(32)) register_13 (.D(WData), .en(demultiplexer_1_out12), .clk(Clock_in), .Q(Q12));  // open: clr
  Register #(.width(32)) register_14 (.D(WData), .en(demultiplexer_1_out13), .clk(Clock_in), .Q(Q13));  // open: clr
  Register #(.width(32)) register_15 (.D(WData), .en(demultiplexer_1_out14), .clk(Clock_in), .Q(Q14));  // open: clr
  Register #(.width(32)) register_16 (.D(WData), .en(demultiplexer_1_out15), .clk(Clock_in), .Q(Q15));  // open: clr
  Register #(.width(32)) register_17 (.D(WData), .en(demultiplexer_1_out16), .clk(Clock_in), .Q(Q16));  // open: clr
  Register #(.width(32)) register_18 (.D(WData), .en(demultiplexer_1_out17), .clk(Clock_in), .Q(Q17));  // open: clr
  Register #(.width(32)) register_19 (.D(WData), .en(demultiplexer_1_out18), .clk(Clock_in), .Q(Q18));  // open: clr
  Register #(.width(32)) register_20 (.D(WData), .en(demultiplexer_1_out19), .clk(Clock_in), .Q(Q19));  // open: clr
  Register #(.width(32)) register_21 (.D(WData), .en(demultiplexer_1_out20), .clk(Clock_in), .Q(Q20));  // open: clr
  Register #(.width(32)) register_22 (.D(WData), .en(demultiplexer_1_out21), .clk(Clock_in), .Q(Q21));  // open: clr
  Register #(.width(32)) register_23 (.D(WData), .en(demultiplexer_1_out22), .clk(Clock_in), .Q(Q22));  // open: clr
  Register #(.width(32)) register_24 (.D(WData), .en(demultiplexer_1_out23), .clk(Clock_in), .Q(Q23));  // open: clr
  Register #(.width(32)) register_25 (.D(WData), .en(demultiplexer_1_out24), .clk(Clock_in), .Q(Q24));  // open: clr
  Register #(.width(32)) register_26 (.D(WData), .en(demultiplexer_1_out25), .clk(Clock_in), .Q(Q25));  // open: clr
  Register #(.width(32)) register_27 (.D(WData), .en(demultiplexer_1_out26), .clk(Clock_in), .Q(Q26));  // open: clr
  Register #(.width(32)) register_28 (.D(WData), .en(demultiplexer_1_out27), .clk(Clock_in), .Q(Q27));  // open: clr
  Register #(.width(32)) register_29 (.D(WData), .en(demultiplexer_1_out28), .clk(Clock_in), .Q(Q28));  // open: clr
  Register #(.width(32)) register_30 (.D(WData), .en(demultiplexer_1_out29), .clk(Clock_in), .Q(Q29));  // open: clr
  Register #(.width(32)) register_31 (.D(WData), .en(demultiplexer_1_out30), .clk(Clock_in), .Q(Q30));  // open: clr
  Register #(.width(32)) register_32 (.D(WData), .en(demultiplexer_1_out31), .clk(Clock_in), .Q(Q31));  // open: clr
  Multiplexer #(.enable("false"), .select(5), .width(32)) multiplexer_1 (
    .in0(Q0), .in1(Q1), .in2(Q2), .in3(Q3), .in4(Q4), .in5(Q5), .in6(Q6), .in7(Q7), .in8(Q8), .in9(Q9),
    .in10(Q10), .in11(Q11), .in12(Q12), .in13(Q13), .in14(Q14), .in15(Q15), .in16(Q16), .in17(Q17),
    .in18(Q18), .in19(Q19), .in20(Q20), .in21(Q21), .in22(Q22), .in23(Q23), .in24(Q24), .in25(Q25),
    .in26(Q26), .in27(Q27), .in28(Q28), .in29(Q29), .in30(Q30), .in31(Q31), .out(R_Data1), .sel(R_Reg1));
  Multiplexer #(.enable("false"), .select(5), .width(32)) multiplexer_2 (
    .in0(Q0), .in1(Q1), .in2(Q2), .in3(Q3), .in4(Q4), .in5(Q5), .in6(Q6), .in7(Q7), .in8(Q8), .in9(Q9),
    .in10(Q10), .in11(Q11), .in12(Q12), .in13(Q13), .in14(Q14), .in15(Q15), .in16(Q16), .in17(Q17),
    .in18(Q18), .in19(Q19), .in20(Q20), .in21(Q21), .in22(Q22), .in23(Q23), .in24(Q24), .in25(Q25),
    .in26(Q26), .in27(Q27), .in28(Q28), .in29(Q29), .in30(Q30), .in31(Q31), .out(R_Data2), .sel(R_Reg2));
endmodule

module register_file_4_32 (
  input  [1:0] RReg1,
  input  [1:0] RReg2,
  input  [31:0] WData,
  input  Clock_in,
  input  Write,
  input  [1:0] WReg,
  output [31:0] RData1,
  output [31:0] RData2
);

  wire demultiplexer_1_out0, demultiplexer_1_out1, demultiplexer_1_out2, demultiplexer_1_out3;
  wire [31:0] register_1_q, register_2_q, register_3_q, register_4_q;

  Demultiplexer #(.enable("false"), .select(2)) demultiplexer_1 (
    .out0(demultiplexer_1_out0), .out1(demultiplexer_1_out1), .out2(demultiplexer_1_out2),
    .out3(demultiplexer_1_out3), .in(Write), .sel(WReg));
  Register #(.width(32)) register_1 (
    .D(WData), .en(demultiplexer_1_out0), .clk(Clock_in), .Q(register_1_q), .clr(Write));
  Register #(.width(32)) register_2 (
    .D(WData), .en(demultiplexer_1_out1), .clk(Clock_in), .Q(register_2_q));  // open: clr
  Register #(.width(32)) register_3 (
    .D(WData), .en(demultiplexer_1_out2), .clk(Clock_in), .Q(register_3_q));  // open: clr
  Register #(.width(32)) register_4 (
    .D(WData), .en(demultiplexer_1_out3), .clk(Clock_in), .Q(register_4_q));  // open: clr
  Multiplexer #(.enable("false"), .select(2), .width(32)) multiplexer_1 (
    .in0(register_1_q), .in1(register_2_q), .in2(register_3_q), .in3(register_4_q), .out(RData1), .sel(RReg1));
  Multiplexer #(.enable("false"), .select(2), .width(32)) multiplexer_2 (
    .in0(register_1_q), .in1(register_2_q), .in2(register_3_q), .in3(register_4_q), .out(RData2), .sel(RReg2));
endmodule

module Reg_test (
  input  [1:0] RReg1,
  input  [1:0] RReg2,
  input  [31:0] WData,
  input  Clock_in,
  input  Write,
  input  [1:0] WReg,
  output [31:0] RData1,
  output [31:0] RData2
);

  wire demultiplexer_1_out0, demultiplexer_1_out1, demultiplexer_1_out2, demultiplexer_1_out3;
  wire [31:0] register_1_q, register_2_q, register_3_q, register_4_q;

  Demultiplexer #(.enable("false"), .select(2)) demultiplexer_1 (
    .out0(demultiplexer_1_out0), .out1(demultiplexer_1_out1), .out2(demultiplexer_1_out2),
    .out3(demultiplexer_1_out3), .in(Write), .sel(WReg));
  Register #(.width(32)) register_1 (
    .D(WData), .en(demultiplexer_1_out0), .clk(Clock_in), .Q(register_1_q));  // open: clr
  Register #(.width(32)) register_2 (
    .D(WData), .en(demultiplexer_1_out1), .clk(Clock_in), .Q(register_2_q));  // open: clr
  Register #(.width(32)) register_3 (
    .D(WData), .en(demultiplexer_1_out2), .clk(Clock_in), .Q(register_3_q));  // open: clr
  Register #(.width(32)) register_4 (
    .D(WData), .en(demultiplexer_1_out3), .clk(Clock_in), .Q(register_4_q));  // open: clr
  Multiplexer #(.enable("false"), .select(2), .width(32)) multiplexer_1 (
    .in0(register_1_q), .in1(register_2_q), .in2(register_3_q), .in3(register_4_q), .out(RData1), .sel(RReg1));
  Multiplexer #(.enable("false"), .select(2), .width(32)) multiplexer_2 (
    .in0(register_1_q), .in1(register_2_q), .in2(register_3_q), .in3(register_4_q), .out(RData2), .sel(RReg2));
endmodule

module ctr (
  input  [6:0] I6,
  output Mtoreg,
  output RWrite,
  output Read,
  output MWrite,
  output Branch
);

  wire not_1_out, not_2_out;

  not not_1 (not_1_out, I6[6]);
  not not_2 (not_2_out, I6[5]);
  not not_3 (Mtoreg, I6[4]);
  or or_1 (RWrite, not_2_out, I6[4]);
  and and_1 (Read, not_2_out, Mtoreg);
  and and_2 (MWrite, not_1_out, Mtoreg, I6[5]);

  assign Branch = I6[6];
endmodule

module DataMem (
  input  [25:0] address,
  input  Write,
  input  Memoryread,
  input  clockin,
  input  [31:0] WD,
  output [31:0] Instr
);

  RAM #(.addrWidth(24), .asyncread("true"), .dataWidth(32)) ram_1 (
    .addr(address[25:2]), .we(Write), .oe(Memoryread), .clk(clockin), .din(WD), .dout(Instr));
endmodule

module In_memory (
  input  [23:0] address,
  input  clock_in,
  output [31:0] Instr
);

  wire not_1_out;

  not not_1 (not_1_out, clock_in);
  RAM #(.addrWidth(22), .asyncread("true"), .dataWidth(32)) ram_1 (
    .addr(address[23:2]), .we(1'b0), .oe(not_1_out), .dout(Instr));  // open: clk, din
endmodule

module mmG (
  input  [31:0] Instr,
  output [31:0] IMM32
);

  Multiplexer #(.enable("false"), .select(2)) multiplexer_1 (
    .in0(Instr[20]), .in1(Instr[7]), .in2(1'b0), .out(IMM32[0]), .sel(Instr[6:5]));  // open: in3
  Multiplexer #(.enable("false"), .width(4)) multiplexer_2 (
    .in0(Instr[24:21]), .in1(Instr[11:8]), .out(IMM32[4:1]), .sel(Instr[5]));
  Multiplexer #(.enable("false")) multiplexer_3 (.in0(Instr[31]), .in1(Instr[7]), .out(IMM32[11]), .sel(Instr[6]));
  assign IMM32[31:12] = {{19{Instr[31]}}, Instr[31]};  // Bit_Extender bit_extender_1

  assign IMM32[10:5] = Instr[30:25];

  // Other names for the same wires on the sheet: I30_25[5:0] = Instr[30:25]; I5 = Instr[5]; I6_5[1:0] = Instr[6:5];
  //   I6 = Instr[6]; I7 = Instr[7]; I11_8[3:0] = Instr[11:8]; I_20 = Instr[20]; I24_21[3:0] = Instr[24:21];
  //   I31 = Instr[31]
endmodule
